// Logisim project 6주차_컴구과제_2020182037정롭비.circ as structural Verilog
// 2x1Mux
module _2x1_Mux (
  input  S,
  input  I0,
  input  I1,
  output out_4
);

  wire and_1_out, and_2_out, not_1_out;

  not not_1 (not_1_out, S);
  and and_1 (and_1_out, not_1_out, I0);
  and and_2 (and_2_out, S, I1);
  or or_1 (out_4, and_1_out, and_2_out);
endmodule

module _4x1_Mux (
  input  S0,
  input  S1,
  input  I0,
  input  I1,
  input  I2,
  input  I3,
  output out_7
);

  wire and_1_out, and_2_out, and_3_out, and_4_out, not_1_out, not_2_out;

  not not_1 (not_1_out, S1);
  not not_2 (not_2_out, S0);
  and and_1 (and_1_out, not_2_out, not_1_out, I0);
  and and_2 (and_2_out, not_2_out, S1, I1);
  and and_3 (and_3_out, S0, not_1_out, I2);
  and and_4 (and_4_out, S0, S1, I3);
  or or_1 (out_7, and_1_out, and_2_out, and_3_out, and_4_out);
endmodule

// 1LU
module _1bit_LU (
  input  A,
  input  B,
  input  S1,
  input  S0,
  output out_5
);

  wire and_1_out, not_1_out, or_1_out, xor_1_out;

  and and_1 (and_1_out, A, B);
  or or_1 (or_1_out, A, B);
  xor xor_1 (xor_1_out, A, B);
  not not_1 (not_1_out, A);
  _4x1_Mux u_4x1_mux_1 (.S0(S1), .S1(S0), .I0(and_1_out), .I1(or_1_out), .I2(xor_1_out), .I3(not_1_out), .out_7(out_5));
endmodule

module _4bit_LU (
  input  [3:0] A,
  input  [3:0] B,
  input  S1,
  input  S0,
  output [3:0] O
);

  _1bit_LU u_1bit_lu_1 (.A(A[0]), .B(B[0]), .S1(S1), .S0(S0), .out_5(O[0]));
  _1bit_LU u_1bit_lu_2 (.A(A[1]), .B(B[1]), .S1(S1), .S0(S0), .out_5(O[1]));
  _1bit_LU u_1bit_lu_3 (.A(A[2]), .B(B[2]), .S1(S1), .S0(S0), .out_5(O[2]));
  _1bit_LU u_1bit_lu_4 (.A(A[3]), .B(B[3]), .S1(S1), .S0(S0), .out_5(O[3]));
endmodule

module _8bit_LU (
  input  [7:0] A,
  input  [7:0] B,
  input  S0,
  input  S1,
  output [7:0] O
);

  _4bit_LU u_4bit_lu_1 (.A(A[3:0]), .B(B[3:0]), .S1(S0), .S0(S1), .O(O[3:0]));
  _4bit_LU u_4bit_lu_2 (.A(A[7:4]), .B(B[7:4]), .S1(S0), .S0(S1), .O(O[7:4]));
endmodule

// 4bit SH
module _4bit_shifter (
  input  SLin,
  input  [3:0] in_2,
  input  N,
  input  SRin,
  input  S0,
  input  S1,
  output Rout,
  output [3:0] Out,
  output Lout
);

  wire and_1_out, not_1_out, or_1_out;

  not not_1 (not_1_out, N);
  or or_1 (or_1_out, SRin, and_1_out);
  and and_1 (and_1_out, not_1_out, in_2[3]);
  _4x1_Mux u_4x1_mux_1 (.S0(S0), .S1(S1), .I0(in_2[0]), .I1(SLin), .I2(in_2[1]), .I3(in_2[1]), .out_7(Out[0]));
  _4x1_Mux u_4x1_mux_2 (.S0(S0), .S1(S1), .I0(in_2[1]), .I1(in_2[0]), .I2(in_2[2]), .I3(in_2[2]), .out_7(Out[1]));
  _4x1_Mux u_4x1_mux_3 (.S0(S0), .S1(S1), .I0(in_2[2]), .I1(in_2[1]), .I2(in_2[3]), .I3(in_2[3]), .out_7(Out[2]));
  _4x1_Mux u_4x1_mux_4 (.S0(S0), .S1(S1), .I0(in_2[3]), .I1(in_2[2]), .I2(SRin), .I3(or_1_out), .out_7(Out[3]));
  and and_2 (Rout, S0, in_2[0]);
  and and_3 (Lout, in_2[3], S1);

  // Notes on the sheet:
  //   S1 S0
  //   0 0 = pass
  //   0 1 = shift left
  //   1 0 = shift right
endmodule

// 8bit shift
module _8bit_shifter (
  input  SLin,
  input  [7:0] in_2,
  input  SRin,
  input  S1,
  input  S0,
  input  N,
  output [7:0] out_7
);

  wire n4bit_shifter_1_lout, n4bit_shifter_2_rout, not_1_out;

  not not_1 (not_1_out, N);
  _4bit_shifter u_4bit_shifter_1 (
    .SLin(SLin), .in_2(in_2[3:0]), .SRin(n4bit_shifter_2_rout), .S0(S1), .S1(S0), .Out(out_7[3:0]),
    .Lout(n4bit_shifter_1_lout), .N(not_1_out));  // open: Rout
  _4bit_shifter u_4bit_shifter_2 (
    .SLin(n4bit_shifter_1_lout), .in_2(in_2[7:4]), .SRin(SRin), .S0(S1), .S1(S0), .Out(out_7[7:4]),
    .Rout(n4bit_shifter_2_rout), .N(N));  // open: Lout

  // Notes on the sheet:
  //   S1 S0
  //   0 0 = pass
  //   0 1 = shift left
  //   1 0 = shift right
endmodule

// FA
module full_adder (
  input  A,
  input  B,
  input  Ci,
  output S,
  output Co
);

  wire and_1_out, and_2_out, and_3_out, and_4_out, and_5_out, and_6_out, and_7_out, not_1_out, not_2_out,
       not_3_out, not_4_out, not_5_out, not_6_out;

  not not_1 (not_1_out, A);
  not not_2 (not_2_out, B);
  not not_3 (not_3_out, A);
  not not_4 (not_4_out, Ci);
  not not_5 (not_5_out, B);
  not not_6 (not_6_out, Ci);
  and and_1 (and_1_out, B, Ci);
  and and_2 (and_2_out, A, Ci);
  and and_3 (and_3_out, A, B);
  and and_4 (and_4_out, not_1_out, not_2_out, Ci);
  and and_5 (and_5_out, not_3_out, B, not_4_out);
  and and_6 (and_6_out, A, not_5_out, not_6_out);
  and and_7 (and_7_out, A, B, Ci);
  or or_1 (Co, and_1_out, and_2_out, and_3_out);
  or or_2 (S, and_4_out, and_5_out, and_6_out, and_7_out);
endmodule

// 1AU
module _1bit_AU (
  input  Ci,
  input  A,
  input  B,
  input  S0,
  input  S1,
  output S,
  output Co
);

  wire n4x1_mux_1_out_7, not_1_out;

  _4x1_Mux u_4x1_mux_1 (.S0(S0), .S1(S1), .I0(1'b0), .I1(B), .I2(not_1_out), .I3(1'b1), .out_7(n4x1_mux_1_out_7));
  not not_1 (not_1_out, B);
  full_adder full_adder_1 (.A(A), .B(n4x1_mux_1_out_7), .Ci(Ci), .S(S), .Co(Co));
endmodule

// 4AU
module _4bit_AU (
  input  Ci,
  input  [3:0] A,
  input  [3:0] B,
  input  S0,
  input  S1,
  output [3:0] S,
  output out_7,
  output Co
);

  wire n1bit_au_1_co, n1bit_au_2_co, n1bit_au_3_co;

  _1bit_AU u_1bit_au_1 (.Ci(Ci), .A(A[0]), .B(B[0]), .S0(S0), .S1(S1), .S(S[0]), .Co(n1bit_au_1_co));
  _1bit_AU u_1bit_au_2 (.Ci(n1bit_au_1_co), .A(A[1]), .B(B[1]), .S0(S0), .S1(S1), .S(S[1]), .Co(n1bit_au_2_co));
  _1bit_AU u_1bit_au_3 (.Ci(n1bit_au_2_co), .A(A[2]), .B(B[2]), .S0(S0), .S1(S1), .S(S[2]), .Co(n1bit_au_3_co));
  _1bit_AU u_1bit_au_4 (.Ci(n1bit_au_3_co), .A(A[3]), .B(B[3]), .S0(S0), .S1(S1), .S(S[3]), .Co(Co));
  xor xor_1 (out_7, n1bit_au_3_co, Co);
endmodule

// 8AU
module _8bit_AU (
  input  Ci,
  input  [7:0] A,
  input  [7:0] B,
  input  S1,
  input  S0,
  output [7:0] F,
  output Z,
  output S,
  output V,
  output Co
);

  wire n1bit_au_1_co, n1bit_au_2_co, n1bit_au_3_co, n1bit_au_4_co, n1bit_au_5_co, n1bit_au_6_co,
       n1bit_au_7_co;

  _1bit_AU u_1bit_au_1 (.Ci(Ci), .A(A[0]), .B(B[0]), .S0(S1), .S1(S0), .S(F[0]), .Co(n1bit_au_1_co));
  _1bit_AU u_1bit_au_2 (.Ci(n1bit_au_1_co), .A(A[1]), .B(B[1]), .S0(S1), .S1(S0), .S(F[1]), .Co(n1bit_au_2_co));
  _1bit_AU u_1bit_au_3 (.Ci(n1bit_au_2_co), .A(A[2]), .B(B[2]), .S0(S1), .S1(S0), .S(F[2]), .Co(n1bit_au_3_co));
  _1bit_AU u_1bit_au_4 (.Ci(n1bit_au_3_co), .A(A[3]), .B(B[3]), .S0(S1), .S1(S0), .S(F[3]), .Co(n1bit_au_4_co));
  _1bit_AU u_1bit_au_5 (.Ci(n1bit_au_4_co), .A(A[4]), .B(B[4]), .S0(S1), .S1(S0), .S(F[4]), .Co(n1bit_au_5_co));
  _1bit_AU u_1bit_au_6 (.Ci(n1bit_au_5_co), .A(A[5]), .B(B[5]), .S0(S1), .S1(S0), .S(F[5]), .Co(n1bit_au_6_co));
  _1bit_AU u_1bit_au_7 (.Ci(n1bit_au_6_co), .A(A[6]), .B(B[6]), .S0(S1), .S1(S0), .S(F[6]), .Co(n1bit_au_7_co));
  _1bit_AU u_1bit_au_8 (.Ci(n1bit_au_7_co), .A(A[7]), .B(B[7]), .S0(S1), .S1(S0), .S(F[7]), .Co(Co));
  xor xor_1 (V, n1bit_au_7_co, Co);
  nor nor_1 (Z, F[0], F[1], F[2], F[3], F[4], F[5], F[6], F[7]);

  assign S = F[7];
endmodule

// 4bit 2x1
module _4bit_2x1mux (
  input  [3:0] A,
  input  [3:0] B,
  input  S,
  output [3:0] out_4
);

  _2x1_Mux u_2x1_mux_1 (.S(S), .I0(A[0]), .I1(B[0]), .out_4(out_4[0]));
  _2x1_Mux u_2x1_mux_2 (.S(S), .I0(A[1]), .I1(B[1]), .out_4(out_4[1]));
  _2x1_Mux u_2x1_mux_3 (.S(S), .I0(A[2]), .I1(B[2]), .out_4(out_4[2]));
  _2x1_Mux u_2x1_mux_4 (.S(S), .I0(A[3]), .I1(B[3]), .out_4(out_4[3]));
endmodule

// 8bit 2x1
module _8bit_2x1mux (
  input  [7:0] A,
  input  [7:0] B,
  input  S,
  output [7:0] out_4
);

  _4bit_2x1mux u_4bit_2x1mux_1 (.A(A[3:0]), .B(B[3:0]), .S(S), .out_4(out_4[3:0]));
  _4bit_2x1mux u_4bit_2x1mux_2 (.A(A[7:4]), .B(B[7:4]), .S(S), .out_4(out_4[7:4]));
endmodule

// 4ALU
module _4bit_ALU (
  input  [3:0] A,
  input  [3:0] B,
  input  S2,
  input  S1,
  input  S0,
  input  Ci,
  output V,
  output Co,
  output Z,
  output S,
  output [3:0] out_11
);

  wire [3:0] n4bit_2x1mux_1_out_4, n4bit_au_1_s, n4bit_lu_1_o, n4bit_shifter_1_out;

  _4bit_AU u_4bit_au_1 (.Ci(Ci), .A(A), .B(B), .S0(S1), .S1(S0), .S(n4bit_au_1_s), .out_7(V), .Co(Co));
  _4bit_LU u_4bit_lu_1 (.A(A), .B(B), .S1(S1), .S0(S0), .O(n4bit_lu_1_o));
  _4bit_shifter u_4bit_shifter_1 (
    .SLin(1'b0), .in_2(A), .SRin(1'b0), .S0(S1), .S1(S0), .Out(n4bit_shifter_1_out));  // open: Rout, Lout, N
  _4bit_2x1mux u_4bit_2x1mux_1 (.A(n4bit_lu_1_o), .B(n4bit_shifter_1_out), .S(Ci), .out_4(n4bit_2x1mux_1_out_4));
  _4bit_2x1mux u_4bit_2x1mux_2 (.A(n4bit_au_1_s), .B(n4bit_2x1mux_1_out_4), .S(S2), .out_4(out_11));
  nor nor_1 (Z, out_11[0], out_11[1], out_11[2], out_11[3]);

  assign S = out_11[3];

  // Notes on the sheet:
  //   S2 == 0 : AU , S2,Ci == 1, 0 : LU    S2, Ci == 1 , 1 : Shift
endmodule

// 8 ALU
module _8bit_ALU (
  input  [7:0] A,
  input  [7:0] B,
  input  S2,
  input  S1,
  input  S0,
  input  Ci,
  output V,
  output Co,
  output Z,
  output S,
  output [7:0] F
);

  wire [7:0] n8bit_2x1mux_1_out_4, n8bit_au_1_f, n8bit_lu_1_o, n8bit_shifter_1_out_7;

  _8bit_AU u_8bit_au_1 (.Ci(Ci), .A(A), .B(B), .S1(S1), .S0(S0), .F(n8bit_au_1_f), .V(V), .Co(Co));  // open: Z, S
  _8bit_LU u_8bit_lu_1 (.A(A), .B(B), .O(n8bit_lu_1_o), .S0(S1), .S1(S0));
  _8bit_shifter u_8bit_shifter_1 (
    .in_2(A), .SRin(1'b0), .S1(S1), .S0(S0), .N(1'b0), .out_7(n8bit_shifter_1_out_7));  // open: SLin
  _8bit_2x1mux u_8bit_2x1mux_1 (.A(n8bit_lu_1_o), .B(n8bit_shifter_1_out_7), .S(Ci), .out_4(n8bit_2x1mux_1_out_4));
  _8bit_2x1mux u_8bit_2x1mux_2 (.A(n8bit_au_1_f), .B(n8bit_2x1mux_1_out_4), .S(S2), .out_4(F));
  nor nor_1 (Z, F[0], F[1], F[2], F[3], F[4], F[5], F[6], F[7]);

  assign S = F[7];
endmodule

// 8 ALU
module _8bit_ALU__4_x_2 (
  input  [7:0] A,
  input  [7:0] B,
  input  S2,
  input  S1,
  input  S0,
  input  Ci,
  output V,
  output Co,
  output Z,
  output [7:0] F,
  output S
);

  wire n4bit_alu_1_co, n4bit_alu_1_z, n4bit_alu_2_z;

  _4bit_ALU u_4bit_alu_1 (
    .A(A[3:0]), .B(B[3:0]), .S1(S1), .S0(S0), .S2(S2), .Ci(Ci), .Co(n4bit_alu_1_co), .Z(n4bit_alu_1_z),
    .out_11(F[3:0]));  // open: V, S
  _4bit_ALU u_4bit_alu_2 (
    .A(A[7:4]), .B(B[7:4]), .S1(S1), .S0(S0), .S2(S2), .Ci(n4bit_alu_1_co), .V(V), .Co(Co),
    .Z(n4bit_alu_2_z), .S(S), .out_11(F[7:4]));
  and and_1 (Z, n4bit_alu_1_z, n4bit_alu_2_z);
endmodule

module uOp (
  input  acld,
  input  [1:0] R,
  input  pcld,
  input  iraddrld,
  input  [3:0] ALU,
  input  mbrld,
  input  stld,
  input  M,
  input  marld,
  input  iropld,
  input  in_11,
  input  rw,
  input  in_13
);

  wire clock_1_out, not_1_out;
  wire [3:0] n8bit_alu_4_x_2_1_v;
  wire [7:0] controlled_buffer_1_out, multiplexer_1_out, multiplexer_2_out, n8bit_alu_4_x_2_1_f,
       register_1_q, register_2_q, register_3_q, register_4_q, register_5_q;

  Multiplexer #(.width(8), .enable("false")) multiplexer_1 (
    .in0(n8bit_alu_4_x_2_1_f), .in1(controlled_buffer_1_out), .out(multiplexer_1_out), .sel(M));
  Clock clock_1 (.out(clock_1_out));
  Register register_1 (.D(n8bit_alu_4_x_2_1_f), .en(acld), .Q(register_1_q), .clk(clock_1_out), .clr(in_11));
  Register register_2 (.D(n8bit_alu_4_x_2_1_f), .en(pcld), .Q(register_2_q), .clk(clock_1_out), .clr(in_11));
  Register register_3 (.D(n8bit_alu_4_x_2_1_f), .en(iraddrld), .Q(register_3_q), .clk(clock_1_out), .clr(in_11));
  Register register_4 (.D(multiplexer_1_out), .en(mbrld), .Q(register_4_q), .clk(clock_1_out), .clr(in_11));
  Register register_5 (.D(n8bit_alu_4_x_2_1_f), .en(marld), .Q(register_5_q), .clk(clock_1_out), .clr(in_11));
  not not_1 (not_1_out, rw);
  Register IR_Op (.D(register_4_q), .en(iropld), .clk(clock_1_out), .clr(in_11));  // open: Q
  assign controlled_buffer_1_out = not_1_out ? register_4_q : 8'bz;  // Controlled_Buffer controlled_buffer_1
  Multiplexer #(.select(2), .width(8), .enable("false")) multiplexer_2 (
    .in0(register_1_q), .in1(register_2_q), .in2(register_3_q), .in3(register_4_q), .out(multiplexer_2_out),
    .sel(R));
  // Probe on multiplexer_2_out
  // Probe on register_4_q
  Register #(.width(4)) Status (.D(n8bit_alu_4_x_2_1_v), .en(stld), .clk(clock_1_out), .clr(in_11));  // open: Q
  _8bit_ALU__4_x_2 u_8bit_alu_4_x_2_1 (
    .A(multiplexer_2_out), .B(register_4_q), .S1(ALU[2]), .S0(ALU[1]), .S2(ALU[3]), .Ci(ALU[0]),
    .V(n8bit_alu_4_x_2_1_v[0]), .Co(n8bit_alu_4_x_2_1_v[1]), .Z(n8bit_alu_4_x_2_1_v[2]),
    .F(n8bit_alu_4_x_2_1_f), .S(n8bit_alu_4_x_2_1_v[3]));
  // Probe on n8bit_alu_4_x_2_1_f
  RAM ram_1 (
    .addr(register_5_q), .data(controlled_buffer_1_out), .sel(in_13), .clk(clock_1_out), .ld(rw));  // open: clr

  // Notes on the sheet:
  //   AC
  //   PC
  //   IR Addr
  //   MBR
  //   MAR
  //   RAM
endmodule
