// Logisim project 2주차.circ as structural Verilog
module SR_Latch (
  input  R,
  input  S,
  input  nS,
  input  nR,
  output Q,
  output nQ,
  output Q_2,
  output nQ_2
);

  nor nor_1 (Q, R, nQ);
  nor nor_2 (nQ, Q, S);
  nand nand_1 (Q_2, nS, nQ_2);
  nand nand_2 (nQ_2, Q_2, nR);
endmodule

module gated_latch (
  input  R,
  input  E,
  input  S,
  output Q,
  output nQ
);

  wire and_1_out, and_2_out;

  and and_1 (and_1_out, R, E);
  and and_2 (and_2_out, E, S);
  nor nor_1 (nQ, Q, and_2_out);
  nor nor_2 (Q, and_1_out, nQ);
endmodule

module D_latch (
  input  D,
  input  E,
  output Q,
  output nQ
);

  wire and_1_out, and_2_out, not_1_out;

  not not_1 (not_1_out, D);
  and and_1 (and_1_out, not_1_out, E);
  and and_2 (and_2_out, E, D);
  nor nor_1 (Q, and_1_out, nQ);
  nor nor_2 (nQ, Q, and_2_out);
endmodule

// D FF
module Master_slave_edge_triggered_D_flip_flop (
  input  D,
  input  Ck,
  output Q,
  output nQ
);

  wire d_latch_1_q, not_1_out;

  D_latch d_latch_1 (.D(D), .E(not_1_out), .Q(d_latch_1_q));  // open: nQ
  not not_1 (not_1_out, Ck);
  D_latch d_latch_2 (.D(d_latch_1_q), .E(Ck), .Q(Q), .nQ(nQ));
endmodule

module _4bit_register (
  input  [3:0] D,
  input  Ck,
  output [3:0] Q
);

  Master_slave_edge_triggered_D_flip_flop master_slave_edge_triggered_d_flip_flop_1 (
    .D(D[0]), .Ck(Ck), .Q(Q[0]));  // open: nQ
  Master_slave_edge_triggered_D_flip_flop master_slave_edge_triggered_d_flip_flop_2 (
    .D(D[1]), .Ck(Ck), .Q(Q[1]));  // open: nQ
  Master_slave_edge_triggered_D_flip_flop master_slave_edge_triggered_d_flip_flop_3 (
    .D(D[2]), .Ck(Ck), .Q(Q[2]));  // open: nQ
  Master_slave_edge_triggered_D_flip_flop master_slave_edge_triggered_d_flip_flop_4 (
    .D(D[3]), .Ck(Ck), .Q(Q[3]));  // open: nQ
endmodule

module _8bit_register (
);

  _4bit_register _4bit ();  // open: D, Ck, Q
  _4bit_register _4bit_2 ();  // open: D, Ck, Q
endmodule
