// Logisim project 3주차.circ as structural Verilog
// I LU
module _1bit_LU (
  input  A,
  input  B,
  input  in_3,
  input  in_4,
  output out_5
);

  wire and_1_out, not_1_out, or_1_out, xor_1_out;

  and and_1 (and_1_out, A, B);
  _4x1_MUX u_4x1_mux_1 (
    .in_1(and_1_out), .in_2(or_1_out), .in_3(xor_1_out), .in_4(not_1_out), .in_5(in_3), .in_6(in_4),
    .out_7(out_5));
  or or_1 (or_1_out, A, B);
  xor xor_1 (xor_1_out, A, B);
  not not_1 (not_1_out, A);
endmodule

// 4 MUX
module _4x1_MUX (
  input  in_1,
  input  in_2,
  input  in_3,
  input  in_4,
  input  in_5,
  input  in_6,
  output out_7
);

  wire and_1_out, and_2_out, and_3_out, and_4_out, not_1_out, not_2_out;

  not not_1 (not_1_out, in_2);
  not not_2 (not_2_out, in_1);
  and and_1 (and_1_out, not_2_out, not_1_out, in_3);
  and and_2 (and_2_out, in_1, not_1_out, in_4);
  and and_3 (and_3_out, not_2_out, in_2, in_5);
  and and_4 (and_4_out, in_1, in_2, in_6);
  or or_1 (out_7, and_1_out, and_2_out, and_3_out, and_4_out);
endmodule

module _4bit_LU (
  input  [3:0] A,
  input  [3:0] B,
  input  in_3,
  input  in_4,
  output [3:0] F
);

  _1bit_LU u_1bit_lu_1 (.A(A[0]), .B(B[0]), .in_3(in_3), .in_4(in_4), .out_5(F[0]));
  _1bit_LU u_1bit_lu_2 (.A(A[1]), .B(B[1]), .in_3(in_3), .in_4(in_4), .out_5(F[1]));
  _1bit_LU u_1bit_lu_3 (.A(A[2]), .B(B[2]), .in_3(in_3), .in_4(in_4), .out_5(F[2]));
  _1bit_LU u_1bit_lu_4 (.A(A[3]), .B(B[3]), .in_3(in_3), .in_4(in_4), .out_5(F[3]));
endmodule

module _4bit_shifter (
  input  in_1,
  input  [3:0] in_2,
  input  in_3,
  input  in_4,
  input  in_5,
  output [3:0] out_6
);

  _4x1_MUX u_4x1_mux_1 (
    .in_1(in_2[0]), .in_2(in_1), .in_3(in_2[1]), .in_5(in_4), .in_6(in_5), .out_7(out_6[0]));  // open: in_4
  _4x1_MUX u_4x1_mux_2 (
    .in_1(in_2[1]), .in_2(in_2[0]), .in_3(in_2[2]), .in_5(in_4), .in_6(in_5), .out_7(out_6[1]));  // open: in_4
  _4x1_MUX u_4x1_mux_3 (
    .in_1(in_2[2]), .in_2(in_2[1]), .in_3(in_2[3]), .in_5(in_4), .out_7(out_6[2]));  // open: in_4, in_6
  _4x1_MUX u_4x1_mux_4 (
    .in_1(in_2[3]), .in_2(in_2[2]), .in_3(in_3), .in_5(in_4), .in_6(in_5), .out_7(out_6[3]));  // open: in_4
endmodule
