// Logisim project 4주차.circ as structural Verilog
// I LU
module _1bit_LU (
  input  A,
  input  B,
  input  in_3,
  input  in_4,
  output out_5
);

  wire and_1_out, not_1_out, or_1_out, xor_1_out;

  and and_1 (and_1_out, A, B);
  _4x1_MUX u_4x1_mux_1 (
    .in_1(and_1_out), .in_2(or_1_out), .in_3(xor_1_out), .in_4(not_1_out), .in_5(in_3), .in_6(in_4),
    .out_7(out_5));
  or or_1 (or_1_out, A, B);
  xor xor_1 (xor_1_out, A, B);
  not not_1 (not_1_out, A);
endmodule

// 4 MUX
module _4x1_MUX (
  input  in_1,
  input  in_2,
  input  in_3,
  input  in_4,
  input  in_5,
  input  in_6,
  output out_7
);

  wire and_1_out, and_2_out, and_3_out, and_4_out, not_1_out, not_2_out;

  not not_1 (not_1_out, in_2);
  not not_2 (not_2_out, in_1);
  and and_1 (and_1_out, not_2_out, not_1_out, in_3);
  and and_2 (and_2_out, in_1, not_1_out, in_4);
  and and_3 (and_3_out, not_2_out, in_2, in_5);
  and and_4 (and_4_out, in_1, in_2, in_6);
  or or_1 (out_7, and_1_out, and_2_out, and_3_out, and_4_out);
endmodule

// 4 LU
module _4bit_LU (
  input  [3:0] A,
  input  [3:0] B,
  input  in_3,
  input  in_4,
  output [3:0] F
);

  _1bit_LU u_1bit_lu_1 (.A(A[0]), .B(B[0]), .in_3(in_3), .in_4(in_4), .out_5(F[0]));
  _1bit_LU u_1bit_lu_2 (.A(A[1]), .B(B[1]), .in_3(in_3), .in_4(in_4), .out_5(F[1]));
  _1bit_LU u_1bit_lu_3 (.A(A[2]), .B(B[2]), .in_3(in_3), .in_4(in_4), .out_5(F[2]));
  _1bit_LU u_1bit_lu_4 (.A(A[3]), .B(B[3]), .in_3(in_3), .in_4(in_4), .out_5(F[3]));
endmodule

// 4bit sh
module _4bit_shifter (
  input  in_1,
  input  [3:0] in_2,
  input  in_3,
  input  in_4,
  input  in_5,
  output [3:0] out_6
);

  _4x1_MUX u_4x1_mux_1 (
    .in_1(in_2[0]), .in_2(in_1), .in_3(in_2[1]), .in_5(in_4), .in_6(in_5), .out_7(out_6[0]));  // open: in_4
  _4x1_MUX u_4x1_mux_2 (
    .in_1(in_2[1]), .in_2(in_2[0]), .in_3(in_2[2]), .in_5(in_4), .in_6(in_5), .out_7(out_6[1]));  // open: in_4
  _4x1_MUX u_4x1_mux_3 (
    .in_1(in_2[2]), .in_2(in_2[1]), .in_3(in_2[3]), .in_5(in_4), .out_7(out_6[2]));  // open: in_4, in_6
  _4x1_MUX u_4x1_mux_4 (
    .in_1(in_2[3]), .in_2(in_2[2]), .in_3(in_3), .in_5(in_4), .in_6(in_5), .out_7(out_6[3]));  // open: in_4
endmodule

// 8 LU
module _8bit_LU (
  input  [7:0] in_1,
  input  [7:0] in_2,
  input  in_3,
  input  in_4,
  output [7:0] out_5
);

  _4bit_LU u_4bit_lu_1 (.A(in_1[3:0]), .B(in_2[3:0]), .in_3(in_3), .in_4(in_4), .F(out_5[3:0]));
  _4bit_LU u_4bit_lu_2 (.A(in_1[7:4]), .B(in_2[7:4]), .in_3(in_3), .in_4(in_4), .F(out_5[7:4]));
endmodule

module _2x1_MUX (
  input  in_1,
  input  in_2,
  input  in_3,
  output out_4
);

  wire and_1_out, and_2_out, not_1_out;

  not not_1 (not_1_out, in_1);
  and and_1 (and_1_out, not_1_out, in_2);
  and and_2 (and_2_out, in_1, in_3);
  or or_1 (out_4, and_1_out, and_2_out);
endmodule

module HA (
  input  A,
  input  B,
  output out_3,
  output out_4
);

  xor xor_1 (out_3, A, B);
  and and_1 (out_4, A, B);
endmodule

module Full_Adder (
  input  A,
  input  B,
  input  Cin,
  output S,
  output Cout
);

  wire ha_1_out_3, ha_1_out_4, ha_2_out_4;

  HA ha_1 (.A(A), .B(B), .out_3(ha_1_out_3), .out_4(ha_1_out_4));
  HA ha_2 (.A(ha_1_out_3), .B(Cin), .out_3(S), .out_4(ha_2_out_4));
  or or_1 (Cout, ha_2_out_4, ha_1_out_4);
endmodule

module _1bit_AU (
  input  in_1,
  input  in_2,
  input  in_3,
  input  in_4,
  input  in_5,
  output out_6,
  output out_7
);

  wire n4x1_mux_1_out_7, not_1_out;

  not not_1 (not_1_out, in_3);
  _4x1_MUX u_4x1_mux_1 (
    .in_1(1'b1), .in_2(in_3), .in_3(not_1_out), .in_4(1'b1), .in_5(in_4), .in_6(in_5),
    .out_7(n4x1_mux_1_out_7));
  Full_Adder full_adder_1 (.A(in_1), .B(in_2), .Cin(n4x1_mux_1_out_7), .S(out_6), .Cout(out_7));
endmodule

// 4 AU
module _4bit_AU (
  input  in_1,
  input  [3:0] in_2,
  input  [3:0] in_3,
  input  in_4,
  input  in_5,
  output [3:0] out_6,
  output out_7,
  output out_8
);

  wire n1bit_au_1_out_7, n1bit_au_2_out_7, n1bit_au_3_out_7;

  _1bit_AU u_1bit_au_1 (
    .in_1(in_1), .in_2(in_2[0]), .in_3(in_3[0]), .in_4(in_4), .in_5(in_5), .out_6(out_6[0]),
    .out_7(n1bit_au_1_out_7));
  _1bit_AU u_1bit_au_2 (
    .in_1(n1bit_au_1_out_7), .in_2(in_2[1]), .in_3(in_3[1]), .in_4(in_4), .in_5(in_5), .out_6(out_6[1]),
    .out_7(n1bit_au_2_out_7));
  _1bit_AU u_1bit_au_3 (
    .in_1(n1bit_au_2_out_7), .in_2(in_2[2]), .in_3(in_3[2]), .in_4(in_4), .in_5(in_5), .out_6(out_6[2]),
    .out_7(n1bit_au_3_out_7));
  _1bit_AU u_1bit_au_4 (
    .in_1(n1bit_au_3_out_7), .in_2(in_2[3]), .in_3(in_3[3]), .in_4(in_4), .in_5(in_5), .out_6(out_6[3]),
    .out_7(out_8));
  xor xor_1 (out_7, n1bit_au_3_out_7, out_8);
endmodule

// 4 2x1
module _4bit_2x1_MUX (
  input  [3:0] in_1,
  input  [3:0] in_2,
  input  in_3,
  output [3:0] out_4
);

  _2x1_MUX u_2x1_mux_1 (.in_1(in_1[0]), .in_2(in_2[0]), .in_3(in_3), .out_4(out_4[0]));
  _2x1_MUX u_2x1_mux_2 (.in_1(in_1[1]), .in_2(in_2[1]), .in_3(in_3), .out_4(out_4[1]));
  _2x1_MUX u_2x1_mux_3 (.in_1(in_1[2]), .in_2(in_2[2]), .in_3(in_3), .out_4(out_4[2]));
  _2x1_MUX u_2x1_mux_4 (.in_1(in_1[3]), .in_2(in_2[3]), .in_3(in_3), .out_4(out_4[3]));
endmodule

module _4bit_ALU (
  input  [3:0] in_1,
  input  [3:0] in_2,
  input  in_3,
  input  in_4,
  input  in_5,
  input  in_6,
  output out_7,
  output out_8,
  output out_9,
  output out_10,
  output [3:0] out_11
);

  wire [3:0] n4bit_2x1_mux_1_out_4, n4bit_au_1_out_6, n4bit_lu_1_f, n4bit_shifter_1_out_6;

  _4bit_AU u_4bit_au_1 (
    .in_1(in_6), .in_2(in_1), .in_3(in_2), .in_4(in_4), .in_5(in_5), .out_6(n4bit_au_1_out_6), .out_7(out_7),
    .out_8(out_8));
  _4bit_LU u_4bit_lu_1 (.A(in_1), .B(in_2), .in_3(in_4), .in_4(in_5), .F(n4bit_lu_1_f));
  _4bit_shifter u_4bit_shifter_1 (
    .in_1(1'b0), .in_2(in_1), .in_3(1'b0), .in_4(in_4), .in_5(in_5), .out_6(n4bit_shifter_1_out_6));
  _4bit_2x1_MUX u_4bit_2x1_mux_1 (
    .in_1(n4bit_lu_1_f), .in_2(n4bit_shifter_1_out_6), .in_3(in_6), .out_4(n4bit_2x1_mux_1_out_4));
  nor nor_1 (out_9, out_11[0], out_11[1], out_11[2], out_10);
  _4bit_2x1_MUX u_4bit_2x1_mux_2 (
    .in_1(n4bit_au_1_out_6), .in_2(n4bit_2x1_mux_1_out_4), .in_3(in_3), .out_4({out_10, out_11[2:0]}));

  assign out_11[3] = out_10;
endmodule
