// Logisim project 5주차.circ as structural Verilog
module \JK_플립플롭  (
  input  in_1,
  input  in_2,
  input  in_3,
  output out_4,
  output out_5
);

  wire and_1_out, and_2_out, and_3_out, and_4_out, nand_1_out, nand_2_out, nor_1_out, nor_2_out, not_1_out;

  nand nand_1 (nand_1_out, out_4, in_2);
  not not_1 (not_1_out, in_3);
  nand nand_2 (nand_2_out, in_1, out_5);
  and and_1 (and_1_out, nand_1_out, in_1, not_1_out);
  and and_2 (and_2_out, not_1_out, in_2, nand_2_out);
  nor nor_1 (nor_1_out, and_1_out, nor_2_out);
  nor nor_2 (nor_2_out, nor_1_out, and_2_out);
  and and_3 (and_3_out, nor_1_out, in_3);
  and and_4 (and_4_out, in_3, nor_2_out);
  nor nor_3 (out_4, and_3_out, out_5);
  nor nor_4 (out_5, out_4, and_4_out);
endmodule

module \_4비트_카운터  (
  output [3:0] out_1
);

  wire and_1_out, and_2_out, clock_1_out;

  Clock clock_1 (.out(clock_1_out));
  and and_1 (and_1_out, out_1[2], and_2_out);
  T_Flip_Flop t_ff_1 (.clk(clock_1_out), .T(and_1_out), .Q(out_1[3]), .en(1'b1));  // open: Qn, preset, reset
  and and_2 (and_2_out, out_1[0], out_1[1]);
  T_Flip_Flop t_ff_2 (.clk(clock_1_out), .T(and_2_out), .Q(out_1[2]), .en(1'b1));  // open: Qn, preset, reset
  T_Flip_Flop t_ff_3 (.clk(clock_1_out), .T(out_1[0]), .Q(out_1[1]), .en(1'b1));  // open: Qn, preset, reset
  T_Flip_Flop t_ff_4 (.clk(clock_1_out), .T(1'b1), .Q(out_1[0]), .en(1'b1));  // open: Qn, preset, reset
endmodule

module \_3x8_디코더  (
  input  in_1,
  input  in_2,
  input  in_3,
  input  in_4,
  output out_5,
  output out_6,
  output out_7,
  output out_8,
  output out_9,
  output out_10,
  output out_11,
  output out_12
);

  wire not_1_out, not_2_out, not_3_out;

  not not_1 (not_1_out, in_1);
  not not_2 (not_2_out, in_2);
  not not_3 (not_3_out, in_3);
  and and_1 (out_5, not_1_out, not_2_out, not_3_out, in_4);
  and and_2 (out_6, not_1_out, not_2_out, in_3, in_4);
  and and_3 (out_7, not_1_out, not_2_out, in_3, in_4);
  and and_4 (out_8, not_1_out, in_2, not_3_out, in_4);
  and and_5 (out_9, in_1, not_2_out, not_3_out, in_4);
  and and_6 (out_10, in_1, not_2_out, not_3_out, in_4);
  and and_7 (out_11, in_1, in_2, not_3_out, in_4);
  and and_8 (out_12, in_1, in_2, in_3, in_4);
endmodule
