// Logisim project 7주차.circ as structural Verilog
module \JK_플립플롭  (
  input  in_1,
  input  in_2,
  input  in_3,
  output out_4,
  output out_5
);

  wire and_1_out, and_2_out, and_3_out, and_4_out, nand_1_out, nand_2_out, nor_1_out, nor_2_out, not_1_out;

  nand nand_1 (nand_1_out, out_4, in_2);
  not not_1 (not_1_out, in_3);
  nand nand_2 (nand_2_out, in_1, out_5);
  and and_1 (and_1_out, nand_1_out, in_1, not_1_out);
  and and_2 (and_2_out, not_1_out, in_2, nand_2_out);
  nor nor_1 (nor_1_out, and_1_out, nor_2_out);
  nor nor_2 (nor_2_out, nor_1_out, and_2_out);
  and and_3 (and_3_out, nor_1_out, in_3);
  and and_4 (and_4_out, in_3, nor_2_out);
  nor nor_3 (out_4, and_3_out, out_5);
  nor nor_4 (out_5, out_4, and_4_out);
endmodule

module \_4비트_카운터  (
  output [3:0] out_1
);

  wire and_1_out, and_2_out, clock_1_out;

  Clock clock_1 (.out(clock_1_out));
  and and_1 (and_1_out, out_1[2], and_2_out);
  T_Flip_Flop t_ff_1 (.clk(clock_1_out), .T(and_1_out), .Q(out_1[3]), .en(1'b1));  // open: Qn, preset, reset
  and and_2 (and_2_out, out_1[0], out_1[1]);
  T_Flip_Flop t_ff_2 (.clk(clock_1_out), .T(and_2_out), .Q(out_1[2]), .en(1'b1));  // open: Qn, preset, reset
  T_Flip_Flop t_ff_3 (.clk(clock_1_out), .T(out_1[0]), .Q(out_1[1]), .en(1'b1));  // open: Qn, preset, reset
  T_Flip_Flop t_ff_4 (.clk(clock_1_out), .T(1'b1), .Q(out_1[0]), .en(1'b1));  // open: Qn, preset, reset
endmodule

module \_3x8_디코더  (
  input  in_1,
  input  in_2,
  input  in_3,
  input  in_4,
  output out_5,
  output out_6,
  output out_7,
  output out_8,
  output out_9,
  output out_10,
  output out_11,
  output out_12
);

  wire not_1_out, not_2_out, not_3_out;

  not not_1 (not_1_out, in_1);
  not not_2 (not_2_out, in_2);
  not not_3 (not_3_out, in_3);
  and and_1 (out_5, not_1_out, not_2_out, not_3_out, in_4);
  and and_2 (out_6, not_1_out, not_2_out, in_3, in_4);
  and and_3 (out_7, not_1_out, in_2, not_3_out, in_4);
  and and_4 (out_8, not_1_out, in_2, in_3, in_4);
  and and_5 (out_9, in_1, not_2_out, not_3_out, in_4);
  and and_6 (out_10, in_1, not_2_out, in_3, in_4);
  and and_7 (out_11, in_1, in_2, not_3_out, in_4);
  and and_8 (out_12, in_1, in_2, in_3, in_4);
endmodule

module \_4x16_디코더  (
  input  in_1,
  input  in_2,
  input  in_3,
  input  in_4,
  input  in_5,
  output out_6,
  output out_7,
  output out_8,
  output out_9,
  output out_10,
  output out_11,
  output out_12,
  output out_13,
  output out_14,
  output out_15,
  output out_16,
  output out_17,
  output out_18,
  output out_19,
  output out_20,
  output out_21
);

  wire and_1_out, and_2_out, not_1_out;

  and and_1 (and_1_out, in_1, not_1_out);
  not not_1 (not_1_out, in_2);
  and and_2 (and_2_out, in_1, in_2);
  \_3x8_디코더  \u_3x8_디코더_1  (
    .in_1(in_3), .in_2(in_4), .in_3(in_5), .in_4(and_1_out), .out_5(out_6), .out_6(out_7), .out_7(out_8),
    .out_8(out_9), .out_9(out_10), .out_10(out_11), .out_11(out_12), .out_12(out_13));
  \_3x8_디코더  \u_3x8_디코더_2  (
    .in_1(in_3), .in_2(in_4), .in_3(in_5), .in_4(and_2_out), .out_5(out_14), .out_6(out_15), .out_7(out_16),
    .out_8(out_17), .out_9(out_18), .out_10(out_19), .out_11(out_20), .out_12(out_21));
endmodule

module \_3x8_디코더____1x8_deMux  (
  input  in_1,
  input  [2:0] in_2,
  input  in_3,
  input  [2:0] in_4,
  output out_5,
  output out_6,
  output out_7,
  output out_8,
  output out_9,
  output out_10,
  output out_11,
  output out_12,
  output out_13,
  output out_14,
  output out_15,
  output out_16,
  output out_17,
  output out_18,
  output out_19,
  output out_20
);

  Demultiplexer #(.select(3), .enable("false")) demultiplexer_1 (
    .out0(out_5), .out1(out_6), .out2(out_7), .out3(out_8), .out4(out_9), .out5(out_10), .out6(out_11),
    .out7(out_12), .in(in_1), .sel(in_2));
  Decoder #(.select(3)) decoder_1 (
    .out0(out_13), .out1(out_14), .out2(out_15), .out3(out_16), .out4(out_17), .out5(out_18), .out6(out_19),
    .out7(out_20), .sel(in_4), .en(in_3));
endmodule

module CPU (
  input  in_1,
  input  [1:0] in_2,
  input  in_3,
  input  [3:0] in_4,
  input  in_5,
  input  in_6,
  input  in_7,
  input  in_8,
  input  in_9,
  input  in_10,
  input  in_11,
  input  in_12,
  input  in_13,
  output [1:0] out_14,
  output [1:0] out_15,
  output [1:0] out_16
);

  wire buffer_1_out, clock_1_out, not_1_out;
  wire [7:0] multiplexer_1_out, n8bit_alu_1_p4, register_1_q, register_3_q, register_5_q, register_6_q,
       register_7_q;
  wire [7:1] register_2_q;
  wire [7:2] n8bit_alu_1_p3, register_4_q;

  Multiplexer #(.enable("false")) multiplexer_1 (
    .in1(buffer_1_out), .out(multiplexer_1_out[0]), .sel(in_8));  // open: in0
  Clock clock_1 (.out(clock_1_out));
  Register register_1 (.D({n8bit_alu_1_p3, out_14}), .en(in_1), .Q(register_1_q), .clk(clock_1_out), .clr(in_11));
  Register register_2 (
    .D({n8bit_alu_1_p3, out_14}), .en(in_3), .Q({register_2_q, in_11}), .clk(clock_1_out), .clr(in_11));
  Register register_3 (.D({n8bit_alu_1_p3, out_14}), .en(in_5), .Q(register_3_q), .clk(clock_1_out), .clr(in_11));
  Register register_4 (.D(multiplexer_1_out), .en(in_6), .Q({register_4_q, out_16}), .clk(clock_1_out), .clr(in_11));
  Register register_5 (.D({n8bit_alu_1_p3, out_14}), .en(in_9), .Q(register_5_q), .clk(clock_1_out), .clr(in_11));
  not not_1 (not_1_out, in_12);
  buf buffer_1 (buffer_1_out, out_16[0]);
  Multiplexer #(.select(2), .width(2), .enable("false")) multiplexer_2 (
    .in0(register_1_q[1:0]), .in1({register_2_q[1], in_11}), .in2(register_3_q[1:0]), .in3(out_16),
    .out(out_15), .sel(in_2));
  // _8BIT_ALU 8bit_alu_1: pin names not known; wires that end beside it: out_15, {register_4_q, out_16}, {n8bit_alu_1_p3, out_14}, n8bit_alu_1_p4[0], n8bit_alu_1_p4[1], n8bit_alu_1_p4[2], n8bit_alu_1_p4[3]
  Register register_6 (.D(n8bit_alu_1_p4), .en(in_7), .Q(register_6_q), .clk(clock_1_out), .clr(in_11));
  Register register_7 (.D({register_4_q, out_16}), .en(in_10), .Q(register_7_q), .clk(clock_1_out), .clr(in_11));
  CU cu_1 ();
  // RAM ram_1: pin names not known; wires that end beside it: register_5_q, in_13, clock_1_out, in_12, buffer_1_out
  // Pins of 2 and 8 bits meet at {n8bit_alu_1_p3, out_14}
  // Pins of 4 and 8 bits meet at n8bit_alu_1_p4
  // Pins of 1 and 2 and 8 bits meet at {register_2_q, in_11}
  // Pins of 1 and 8 bits meet at multiplexer_1_out
  // Pins of 2 and 8 bits meet at register_3_q
  // Pins of 2 and 8 bits meet at register_1_q
  // Pins of 1 and 2 and 8 bits meet at {register_4_q, out_16}
endmodule

module _8BIT_ALU (
  input  [7:0] in_1,
  input  [7:0] in_2
);


  // Notes on the sheet:
  //   A
  //   B
endmodule

module _8AU (
  input  [7:0] in_1,
  input  [7:0] in_2
);
endmodule
