// Logisim project 기말 과제.circ as structural Verilog
module \JK_플립플롭  (
  input  in_1,
  input  in_2,
  input  in_3,
  output out_4,
  output out_5
);

  wire and_1_out, and_2_out, and_3_out, and_4_out, nand_1_out, nand_2_out, nor_1_out, nor_2_out, not_1_out;

  nand nand_1 (nand_1_out, out_4, in_2);
  not not_1 (not_1_out, in_3);
  nand nand_2 (nand_2_out, in_1, out_5);
  and and_1 (and_1_out, nand_1_out, in_1, not_1_out);
  and and_2 (and_2_out, not_1_out, in_2, nand_2_out);
  nor nor_1 (nor_1_out, and_1_out, nor_2_out);
  nor nor_2 (nor_2_out, nor_1_out, and_2_out);
  and and_3 (and_3_out, nor_1_out, in_3);
  and and_4 (and_4_out, in_3, nor_2_out);
  nor nor_3 (out_4, and_3_out, out_5);
  nor nor_4 (out_5, out_4, and_4_out);
endmodule

module \_4비트_카운터  (
  output [3:0] out_1
);

  wire and_1_out, and_2_out, clock_1_out;

  Clock clock_1 (.out(clock_1_out));
  and and_1 (and_1_out, out_1[2], and_2_out);
  T_Flip_Flop t_ff_1 (.clk(clock_1_out), .T(and_1_out), .Q(out_1[3]), .en(1'b1));  // open: Qn, preset, reset
  and and_2 (and_2_out, out_1[0], out_1[1]);
  T_Flip_Flop t_ff_2 (.clk(clock_1_out), .T(and_2_out), .Q(out_1[2]), .en(1'b1));  // open: Qn, preset, reset
  T_Flip_Flop t_ff_3 (.clk(clock_1_out), .T(out_1[0]), .Q(out_1[1]), .en(1'b1));  // open: Qn, preset, reset
  T_Flip_Flop t_ff_4 (.clk(clock_1_out), .T(1'b1), .Q(out_1[0]), .en(1'b1));  // open: Qn, preset, reset
endmodule

module \_3x8_디코더  (
  input  in_1,
  input  in_2,
  input  in_3,
  input  in_4,
  output out_5,
  output out_6,
  output out_7,
  output out_8,
  output out_9,
  output out_10,
  output out_11,
  output out_12
);

  wire not_1_out, not_2_out, not_3_out;

  not not_1 (not_1_out, in_1);
  not not_2 (not_2_out, in_2);
  not not_3 (not_3_out, in_3);
  and and_1 (out_5, not_1_out, not_2_out, not_3_out, in_4);
  and and_2 (out_6, not_1_out, not_2_out, in_3, in_4);
  and and_3 (out_7, not_1_out, in_2, not_3_out, in_4);
  and and_4 (out_8, not_1_out, in_2, in_3, in_4);
  and and_5 (out_9, in_1, not_2_out, not_3_out, in_4);
  and and_6 (out_10, in_1, not_2_out, in_3, in_4);
  and and_7 (out_11, in_1, in_2, not_3_out, in_4);
  and and_8 (out_12, in_1, in_2, in_3, in_4);
endmodule

module \_4x16_디코더  (
  input  in_1,
  input  in_2,
  input  in_3,
  input  in_4,
  input  in_5,
  output out_6,
  output out_7,
  output out_8,
  output out_9,
  output out_10,
  output out_11,
  output out_12,
  output out_13,
  output out_14,
  output out_15,
  output out_16,
  output out_17,
  output out_18,
  output out_19,
  output out_20,
  output out_21
);

  wire and_1_out, and_2_out, not_1_out;

  and and_1 (and_1_out, in_1, not_1_out);
  not not_1 (not_1_out, in_2);
  and and_2 (and_2_out, in_1, in_2);
  \_3x8_디코더  \u_3x8_디코더_1  (
    .in_1(in_3), .in_2(in_4), .in_3(in_5), .in_4(and_1_out), .out_5(out_6), .out_6(out_7), .out_7(out_8),
    .out_8(out_9), .out_9(out_10), .out_10(out_11), .out_11(out_12), .out_12(out_13));
  \_3x8_디코더  \u_3x8_디코더_2  (
    .in_1(in_3), .in_2(in_4), .in_3(in_5), .in_4(and_2_out), .out_5(out_14), .out_6(out_15), .out_7(out_16),
    .out_8(out_17), .out_9(out_18), .out_10(out_19), .out_11(out_20), .out_12(out_21));
endmodule

module \_3x8_디코더____1x8_deMux  (
  input  in_1,
  input  [2:0] in_2,
  input  in_3,
  input  [2:0] in_4,
  output out_5,
  output out_6,
  output out_7,
  output out_8,
  output out_9,
  output out_10,
  output out_11,
  output out_12,
  output out_13,
  output out_14,
  output out_15,
  output out_16,
  output out_17,
  output out_18,
  output out_19,
  output out_20
);

  Demultiplexer #(.select(3), .enable("false")) demultiplexer_1 (
    .out0(out_5), .out1(out_6), .out2(out_7), .out3(out_8), .out4(out_9), .out5(out_10), .out6(out_11),
    .out7(out_12), .in(in_1), .sel(in_2));
  Decoder #(.select(3)) decoder_1 (
    .out0(out_13), .out1(out_14), .out2(out_15), .out3(out_16), .out4(out_17), .out5(out_18), .out6(out_19),
    .out7(out_20), .sel(in_4), .en(in_3));
endmodule

module _8BIT_ALU (
  input  [7:0] A,
  input  [7:0] B,
  input  S2,
  input  S1,
  input  S0,
  input  Ci,
  output V,
  output Co,
  output Z,
  output S,
  output [7:0] F
);

  wire [7:0] n8au_1_f, n8bit_shift_1_out_7, n8lu_1_o;

  _8LU u_8lu_1 (.A(A), .B(B), .O(n8lu_1_o), .in_3(S1), .in_4(S0));
  _8BIT_Shift u_8bit_shift_1 (
    .in_2(A), .in_3(1'b0), .in_4(S1), .in_5(S0), .in_6(1'b0), .out_7(n8bit_shift_1_out_7));  // open: in_1
  _8AU u_8au_1 (.in_1(Ci), .A(A), .B(B), .S1(S1), .S0(S0), .F(n8au_1_f), .out_9(V), .out_10(Co));  // open: Z, S
  nor nor_1 (Z, F[0], F[1], F[2], F[3], F[4], F[5], F[6], F[7]);

  assign S = F[7];
endmodule

module _8AU (
  input  in_1,
  input  [7:0] A,
  input  [7:0] B,
  input  S1,
  input  S0,
  output [7:0] F,
  output Z,
  output S,
  output out_9,
  output out_10
);

  wire n1bit_au_1_c, n1bit_au_2_c, n1bit_au_3_c, n1bit_au_4_c, n1bit_au_5_c, n1bit_au_6_c, n1bit_au_7_c;

  _1BIT_AU u_1bit_au_1 (.Ci(in_1), .A(A[0]), .B(B[0]), .in_4(S1), .in_5(S0), .S(F[0]), .C(n1bit_au_1_c));
  _1BIT_AU u_1bit_au_2 (.Ci(n1bit_au_1_c), .A(A[1]), .B(B[1]), .in_4(S1), .in_5(S0), .S(F[1]), .C(n1bit_au_2_c));
  _1BIT_AU u_1bit_au_3 (.Ci(n1bit_au_2_c), .A(A[2]), .B(B[2]), .in_4(S1), .in_5(S0), .S(F[2]), .C(n1bit_au_3_c));
  _1BIT_AU u_1bit_au_4 (.Ci(n1bit_au_3_c), .A(A[3]), .B(B[3]), .in_4(S1), .in_5(S0), .S(F[3]), .C(n1bit_au_4_c));
  _1BIT_AU u_1bit_au_5 (.Ci(n1bit_au_4_c), .A(A[4]), .B(B[4]), .in_4(S1), .in_5(S0), .S(F[4]), .C(n1bit_au_5_c));
  _1BIT_AU u_1bit_au_6 (.Ci(n1bit_au_5_c), .A(A[5]), .B(B[5]), .in_4(S1), .in_5(S0), .S(F[5]), .C(n1bit_au_6_c));
  _1BIT_AU u_1bit_au_7 (.Ci(n1bit_au_6_c), .A(A[6]), .B(B[6]), .in_4(S1), .in_5(S0), .S(F[6]), .C(n1bit_au_7_c));
  _1BIT_AU u_1bit_au_8 (.Ci(n1bit_au_7_c), .A(A[7]), .B(B[7]), .in_4(S1), .in_5(S0), .S(F[7]), .C(out_10));
  xor xor_1 (out_9, n1bit_au_7_c, out_10);
  nor nor_1 (Z, F[0], F[1], F[2], F[3], F[4], F[5], F[6], F[7]);

  assign S = F[7];
endmodule

module CU (
);

  Decoder decoder_1 ();  // open: out0, out1, sel, en
endmodule

module _4BIT_ALU (
  input  [3:0] in_1,
  input  [3:0] in_2,
  input  in_3,
  input  in_4,
  input  in_5,
  input  in_6
);

  _4BIT_AU u_4bit_au_1 ();  // open: Ci, A, B, S0, S1, out_6, out_7, out_8
endmodule

module _1BIT_AU (
  input  Ci,
  input  A,
  input  B,
  input  in_4,
  input  in_5,
  output S,
  output C
);

  wire n4x1_mux_1_out_7, not_1_out;

  _4x1_MUX u_4x1_mux_1 (
    .S0(1'b0), .S1(B), .in_3(not_1_out), .in_4(1'b1), .in_5(in_4), .in_6(in_5), .out_7(n4x1_mux_1_out_7));
  not not_1 (not_1_out, B);
  full_adder full_adder_1 (.A(A), .B(n4x1_mux_1_out_7), .Ci(Ci), .S(S), .Co(C));
endmodule

module _4x1_MUX (
  input  S0,
  input  S1,
  input  in_3,
  input  in_4,
  input  in_5,
  input  in_6,
  output out_7
);

  wire and_1_out, and_2_out, and_3_out, and_4_out, not_1_out, not_2_out;

  not not_1 (not_1_out, S1);
  not not_2 (not_2_out, S0);
  and and_1 (and_1_out, not_2_out, not_1_out, in_3);
  and and_2 (and_2_out, not_2_out, S1, in_4);
  and and_3 (and_3_out, S0, not_1_out, in_5);
  and and_4 (and_4_out, S0, S1, in_6);
  or or_1 (out_7, and_1_out, and_2_out, and_3_out, and_4_out);
endmodule

module _4BIT_AU (
  input  Ci,
  input  [3:0] A,
  input  [3:0] B,
  input  S0,
  input  S1,
  output [3:0] out_6,
  output out_7,
  output out_8
);

  wire n1bit_au_1_c, n1bit_au_2_c, n1bit_au_3_c;

  _1BIT_AU u_1bit_au_1 (.Ci(Ci), .A(A[0]), .B(B[0]), .in_4(S0), .in_5(S1), .S(out_6[0]), .C(n1bit_au_1_c));
  _1BIT_AU u_1bit_au_2 (.Ci(n1bit_au_1_c), .A(A[1]), .B(B[1]), .in_4(S0), .in_5(S1), .S(out_6[1]), .C(n1bit_au_2_c));
  _1BIT_AU u_1bit_au_3 (.Ci(n1bit_au_2_c), .A(A[2]), .B(B[2]), .in_4(S0), .in_5(S1), .S(out_6[2]), .C(n1bit_au_3_c));
  _1BIT_AU u_1bit_au_4 (.Ci(n1bit_au_3_c), .A(A[3]), .B(B[3]), .in_4(S0), .in_5(S1), .S(out_6[3]), .C(out_8));
  xor xor_1 (out_7, n1bit_au_3_c, out_8);
endmodule

module _4BIT_Shift (
  input  in_1,
  input  [3:0] in_2,
  input  in_3,
  input  in_4,
  input  in_5,
  input  in_6,
  output out_7,
  output [3:0] out_8,
  output out_9
);

  wire and_1_out, not_1_out, or_1_out;

  not not_1 (not_1_out, in_3);
  or or_1 (or_1_out, in_4, and_1_out);
  and and_1 (and_1_out, not_1_out, in_2[3]);
  and and_2 (out_7, in_5, in_2[0]);
  _4x1_MUX u_4x1_mux_1 (
    .S0(in_2[0]), .S1(in_1), .in_3(in_2[1]), .in_4(in_2[1]), .in_5(in_5), .in_6(in_6), .out_7(out_8[0]));
  _4x1_MUX u_4x1_mux_2 (
    .S0(in_2[1]), .S1(in_2[0]), .in_3(in_2[2]), .in_4(in_2[2]), .in_5(in_5), .in_6(in_6), .out_7(out_8[1]));
  _4x1_MUX u_4x1_mux_3 (
    .S0(in_2[2]), .S1(in_2[1]), .in_3(in_2[3]), .in_4(in_2[3]), .in_5(in_5), .in_6(in_6), .out_7(out_8[2]));
  _4x1_MUX u_4x1_mux_4 (
    .S0(in_2[3]), .S1(in_2[2]), .in_3(in_4), .in_4(or_1_out), .in_5(in_5), .in_6(in_6), .out_7(out_8[3]));
  and and_3 (out_9, in_2[3], in_6);
endmodule

module _1LU (
  input  A,
  input  B,
  input  in_3,
  input  in_4,
  output out_5
);

  wire and_1_out, not_1_out, or_1_out, xor_1_out;

  and and_1 (and_1_out, A, A);
  or or_1 (or_1_out, A, A);
  xor xor_1 (xor_1_out, A, A);
  not not_1 (not_1_out, A);
  _4x1_MUX u_4x1_mux_1 (
    .S0(and_1_out), .S1(or_1_out), .in_3(xor_1_out), .in_4(not_1_out), .in_5(in_3), .in_6(in_4), .out_7(out_5));

  assign B = A;
endmodule

module _4LU (
  input  [3:0] A,
  input  [3:0] B,
  input  in_3,
  input  in_4,
  output [3:0] out_5
);

  _1LU u_1lu_1 (.A(A[0]), .B(B[0]), .in_3(in_3), .in_4(in_4), .out_5(out_5[0]));
  _1LU u_1lu_2 (.A(A[1]), .B(B[1]), .in_3(in_3), .in_4(in_4), .out_5(out_5[1]));
  _1LU u_1lu_3 (.A(A[2]), .B(B[2]), .in_3(in_3), .in_4(in_4), .out_5(out_5[2]));
  _1LU u_1lu_4 (.A(A[3]), .B(B[3]), .in_3(in_3), .in_4(in_4), .out_5(out_5[3]));
endmodule

module _8LU (
  input  [7:0] A,
  input  [7:0] B,
  input  in_3,
  input  in_4,
  output [7:0] O
);

  _4LU u_4lu_1 (.A(A[3:0]), .B(B[3:0]), .in_3(in_3), .in_4(in_4), .out_5(O[3:0]));
  _4LU u_4lu_2 (.A(A[7:4]), .B(B[7:4]), .in_3(in_3), .in_4(in_4), .out_5(O[7:4]));
endmodule

module _8BIT_Shift (
  input  in_1,
  input  [7:0] in_2,
  input  in_3,
  input  in_4,
  input  in_5,
  input  in_6,
  output [7:0] out_7
);

  wire n4bit_shift_1_out_7, n4bit_shift_2_out_9, not_1_out;

  not not_1 (not_1_out, in_6);
  _4BIT_Shift u_4bit_shift_1 (
    .in_1(in_1), .in_2(in_2[3:0]), .in_3(not_1_out), .in_4(n4bit_shift_2_out_9), .in_5(in_4), .in_6(in_5),
    .out_7(n4bit_shift_1_out_7), .out_8(out_7[3:0]));  // open: out_9
  _4BIT_Shift u_4bit_shift_2 (
    .in_1(n4bit_shift_1_out_7), .in_2(in_2[7:4]), .in_3(in_6), .in_4(in_3), .in_5(in_4), .in_6(in_5),
    .out_8(out_7[7:4]), .out_9(n4bit_shift_2_out_9));  // open: out_7
endmodule

module _2x1_Mux (
  input  in_1,
  input  in_2,
  input  in_3,
  output out_4
);

  wire and_1_out, and_2_out, not_1_out;

  not not_1 (not_1_out, in_1);
  and and_1 (and_1_out, not_1_out, in_2);
  and and_2 (and_2_out, in_1, in_3);
  or or_1 (out_4, and_1_out, and_2_out);
endmodule

module CPU (
  input  in_1,
  input  [1:0] in_2,
  input  in_3,
  input  [3:0] in_4,
  input  in_5,
  input  in_6,
  input  in_7,
  input  in_8,
  input  in_9,
  input  in_10,
  input  in_11,
  input  in_12,
  input  in_13,
  output [1:0] out_14,
  output [1:0] out_15
);

  wire buffer_1_out, clock_1_out, not_1_out;
  wire [7:0] multiplexer_1_out, n8bit_alu_1_p5, register_1_q, register_3_q, register_4_q, register_5_q,
       register_6_q, register_7_q;
  wire [7:1] register_2_q;
  wire [7:2] n8bit_alu_1_p4;

  Multiplexer #(.enable("false")) multiplexer_1 (
    .in1(buffer_1_out), .out(multiplexer_1_out[0]), .sel(in_8));  // open: in0
  Clock clock_1 (.out(clock_1_out));
  Register register_1 (.D({n8bit_alu_1_p4, out_14}), .en(in_1), .Q(register_1_q), .clk(clock_1_out), .clr(in_11));
  Register register_2 (
    .D({n8bit_alu_1_p4, out_14}), .en(in_3), .Q({register_2_q, in_11}), .clk(clock_1_out), .clr(in_11));
  Register register_3 (.D({n8bit_alu_1_p4, out_14}), .en(in_5), .Q(register_3_q), .clk(clock_1_out), .clr(in_11));
  Register register_4 (.D(multiplexer_1_out), .en(in_6), .Q(register_4_q), .clk(clock_1_out), .clr(in_11));
  Register register_5 (.D({n8bit_alu_1_p4, out_14}), .en(in_9), .Q(register_5_q), .clk(clock_1_out), .clr(in_11));
  buf buffer_1 (buffer_1_out, register_4_q[0]);
  not not_1 (not_1_out, in_12);
  Register register_6 (.D(register_4_q), .en(in_10), .Q(register_6_q), .clk(clock_1_out), .clr(in_11));
  Multiplexer #(.select(2), .width(2), .enable("false")) multiplexer_2 (
    .in0(register_1_q[1:0]), .in1({register_2_q[1], in_11}), .in2(register_3_q[1:0]),
    .in3(register_4_q[1:0]), .out(out_15), .sel(in_2));
  // _8BIT_ALU 8bit_alu_1: pin names not known; wires that end beside it: out_15, out_15, register_4_q, {n8bit_alu_1_p4, out_14}, n8bit_alu_1_p5[0], n8bit_alu_1_p5[1], n8bit_alu_1_p5[2], n8bit_alu_1_p5[3]
  Register register_7 (.D(n8bit_alu_1_p5), .en(in_7), .Q(register_7_q), .clk(clock_1_out), .clr(in_11));
  CU cu_1 ();
  // RAM ram_1: pin names not known; wires that end beside it: register_5_q, in_13, clock_1_out, in_12, buffer_1_out
  // Pins of 1 and 2 and 8 bits meet at {register_2_q, in_11}
  // Pins of 2 and 8 bits meet at {n8bit_alu_1_p4, out_14}
  // Pins of 2 and 8 bits meet at register_1_q
  // Pins of 2 and 8 bits meet at register_3_q
  // Pins of 1 and 2 and 8 bits meet at register_4_q
  // Pins of 1 and 8 bits meet at multiplexer_1_out
  // Pins of 4 and 8 bits meet at n8bit_alu_1_p5
endmodule
