// Logisim project 비트 계산기.circ as structural Verilog
// HA
module half_adder (
  input  A,
  input  B,
  output out_3,
  output out_4
);

  xor xor_1 (out_3, A, B);
  and and_1 (out_4, A, B);
endmodule

// FA
module full_adder (
  input  A,
  input  B,
  input  Cin,
  output S,
  output Cout
);

  wire half_adder_1_out_3, half_adder_1_out_4, half_adder_2_out_4;

  half_adder half_adder_1 (.A(A), .B(B), .out_3(half_adder_1_out_3), .out_4(half_adder_1_out_4));
  half_adder half_adder_2 (.A(half_adder_1_out_3), .B(Cin), .out_3(S), .out_4(half_adder_2_out_4));
  or or_1 (Cout, half_adder_2_out_4, half_adder_1_out_4);
endmodule

// A
module _4bit_adder (
  input  in_1,
  input  [3:0] A,
  input  [3:0] B,
  output [3:0] _8_4_2_1,
  output Cout
);

  wire full_adder_1_cout, full_adder_2_cout, full_adder_3_cout;

  full_adder full_adder_1 (.A(A[0]), .B(B[0]), .Cin(in_1), .S(_8_4_2_1[0]), .Cout(full_adder_1_cout));
  full_adder full_adder_2 (.A(A[1]), .B(B[1]), .Cin(full_adder_1_cout), .S(_8_4_2_1[1]), .Cout(full_adder_2_cout));
  full_adder full_adder_3 (.A(A[2]), .B(B[2]), .Cin(full_adder_2_cout), .S(_8_4_2_1[2]), .Cout(full_adder_3_cout));
  full_adder full_adder_4 (.A(A[3]), .B(B[3]), .Cin(full_adder_3_cout), .S(_8_4_2_1[3]), .Cout(Cout));

  // Notes on the sheet:
  //   8 4 2 1
  //   8 4 2 1
endmodule

module _16bit_adder (
  input  in_1,
  input  [15:0] in_2,
  input  [15:0] in_3,
  output [15:0] out_4,
  output out_5
);

  wire full_adder_1_cout, full_adder_2_cout, full_adder_3_cout, full_adder_4_cout, full_adder_5_cout,
       full_adder_6_cout, full_adder_7_cout, full_adder_8_cout, full_adder_9_cout, full_adder_10_cout,
       full_adder_11_cout, full_adder_12_cout, full_adder_13_cout, full_adder_14_cout, full_adder_15_cout;

  full_adder full_adder_1 (.A(in_2[0]), .B(in_3[0]), .Cin(in_1), .S(out_4[0]), .Cout(full_adder_1_cout));
  full_adder full_adder_2 (.A(in_2[1]), .B(in_3[1]), .Cin(full_adder_1_cout), .S(out_4[1]), .Cout(full_adder_2_cout));
  full_adder full_adder_3 (.A(in_2[2]), .B(in_3[2]), .Cin(full_adder_2_cout), .S(out_4[2]), .Cout(full_adder_3_cout));
  full_adder full_adder_4 (.A(in_2[3]), .B(in_3[3]), .Cin(full_adder_3_cout), .S(out_4[3]), .Cout(full_adder_4_cout));
  full_adder full_adder_5 (.A(in_2[4]), .B(in_3[4]), .Cin(full_adder_4_cout), .S(out_4[4]), .Cout(full_adder_5_cout));
  full_adder full_adder_6 (.A(in_2[5]), .B(in_3[5]), .Cin(full_adder_5_cout), .S(out_4[5]), .Cout(full_adder_6_cout));
  full_adder full_adder_7 (.A(in_2[6]), .B(in_3[6]), .Cin(full_adder_6_cout), .S(out_4[6]), .Cout(full_adder_7_cout));
  full_adder full_adder_8 (.A(in_2[7]), .B(in_3[7]), .Cin(full_adder_7_cout), .S(out_4[7]), .Cout(full_adder_8_cout));
  full_adder full_adder_9 (.A(in_2[8]), .B(in_3[8]), .Cin(full_adder_8_cout), .S(out_4[8]), .Cout(full_adder_9_cout));
  full_adder full_adder_10 (.A(in_2[9]), .B(in_3[9]), .Cin(full_adder_9_cout), .S(out_4[9]), .Cout(full_adder_10_cout));
  full_adder full_adder_11 (
    .A(in_2[10]), .B(in_3[10]), .Cin(full_adder_10_cout), .S(out_4[10]), .Cout(full_adder_11_cout));
  full_adder full_adder_12 (
    .A(in_2[11]), .B(in_3[11]), .Cin(full_adder_11_cout), .S(out_4[11]), .Cout(full_adder_12_cout));
  full_adder full_adder_13 (
    .A(in_2[12]), .B(in_3[12]), .Cin(full_adder_12_cout), .S(out_4[12]), .Cout(full_adder_13_cout));
  full_adder full_adder_14 (
    .A(in_2[13]), .B(in_3[13]), .Cin(full_adder_13_cout), .S(out_4[13]), .Cout(full_adder_14_cout));
  full_adder full_adder_15 (
    .A(in_2[14]), .B(in_3[14]), .Cin(full_adder_14_cout), .S(out_4[14]), .Cout(full_adder_15_cout));
  full_adder full_adder_16 (.A(in_2[15]), .B(in_3[15]), .Cin(full_adder_15_cout), .S(out_4[15]), .Cout(out_5));
endmodule

module _16bit_adder2 (
  input  in_1,
  input  [15:0] in_2,
  input  [15:0] in_3,
  output [15:0] out_4,
  output out_5
);

  wire n4bit_adder_1_cout, n4bit_adder_2_cout, n4bit_adder_3_cout;

  _4bit_adder u_4bit_adder_1 (
    .in_1(in_1), .A(in_2[3:0]), .B(in_3[3:0]), ._8_4_2_1(out_4[3:0]), .Cout(n4bit_adder_1_cout));
  _4bit_adder u_4bit_adder_2 (
    .in_1(n4bit_adder_1_cout), .A(in_2[7:4]), .B(in_3[7:4]), ._8_4_2_1(out_4[7:4]), .Cout(n4bit_adder_2_cout));
  _4bit_adder u_4bit_adder_3 (
    .in_1(n4bit_adder_2_cout), .A(in_2[11:8]), .B(in_3[11:8]), ._8_4_2_1(out_4[11:8]),
    .Cout(n4bit_adder_3_cout));
  _4bit_adder u_4bit_adder_4 (
    .in_1(n4bit_adder_3_cout), .A(in_2[15:12]), .B(in_3[15:12]), ._8_4_2_1(out_4[15:12]), .Cout(out_5));
endmodule
